// Logisim project Mod2Counter.circ as structural Verilog: 1 circuit, main circuit Mod2Counter
module Mod2Counter (
  output out_1
);

  wire clock_1_out, d_ff_1_qn;

  Clock clock_1 (.out(clock_1_out));
  D_Flip_Flop d_ff_1 (.D(d_ff_1_qn), .clk(clock_1_out), .Q(out_1), .Qn(d_ff_1_qn));  // open: preset, reset
endmodule
