// Logisim project Mod4Counter.circ as structural Verilog: 1 circuit, main circuit test
module test (
  input  X,
  output Out1,
  output Out0
);

  wire clock_1_out, not_1_out, xnor_1_out, xor_1_out;

  Clock clock_1 (.out(clock_1_out));
  xor xor_1 (xor_1_out, Out0, Out1);
  xnor xnor_1 (xnor_1_out, xor_1_out, X);
  D_Flip_Flop Q1 (.D(xnor_1_out), .clk(clock_1_out), .Q(Out1));  // open: Qn, preset, reset
  D_Flip_Flop Q0 (.D(not_1_out), .clk(clock_1_out), .Q(Out0));  // open: Qn, preset, reset
  not not_1 (not_1_out, Out0);
endmodule
