// Logisim project readwriteramtied.circ as structural Verilog: 1 circuit, main circuit main
module main (
  output Q1,
  output Q0
);

  wire and_1_out, clock_1_out, d_ff_2_qn, dipswitch_1_sw1, dipswitch_1_sw2, dipswitch_1_sw3, dipswitch_1_sw4,
       dipswitch_2_sw1, dipswitch_2_sw2, dipswitch_2_sw3, dipswitch_2_sw4, multiplexer_1_out,
       multiplexer_2_out, multiplexer_3_out, multiplexer_4_out, not_1_out, not_2_out, Q0R, Q0W, Q1W,
       READ_out, undriven, Write_out, xor_1_out, xor_2_out, xor_3_out;
  wire [0:0] or_1_out;
  wire [3:0] ram_1_data, RegisterA_q, RegisterB_q;

  DipSwitch #(.number(4)) dipswitch_1 (
    .sw1(dipswitch_1_sw1), .sw2(dipswitch_1_sw2), .sw3(dipswitch_1_sw3), .sw4(dipswitch_1_sw4));
  DipSwitch #(.number(4)) dipswitch_2 (
    .sw1(dipswitch_2_sw1), .sw2(dipswitch_2_sw2), .sw3(dipswitch_2_sw3), .sw4(dipswitch_2_sw4));
  Button Write (.out(Write_out));
  Clock clock_1 (.out(clock_1_out));
  Button READ (.out(READ_out));
  Multiplexer multiplexer_1 (.in0(dipswitch_1_sw1), .in1(dipswitch_2_sw1), .out(multiplexer_1_out), .sel(or_1_out[0]));
  Multiplexer multiplexer_2 (.in0(dipswitch_1_sw2), .in1(dipswitch_2_sw2), .out(multiplexer_2_out), .sel(or_1_out[0]));
  Multiplexer multiplexer_3 (.in0(dipswitch_1_sw3), .in1(dipswitch_2_sw3), .out(multiplexer_3_out), .sel(or_1_out[0]));
  Multiplexer multiplexer_4 (.in0(dipswitch_1_sw4), .in1(dipswitch_2_sw4), .out(multiplexer_4_out), .sel(or_1_out[0]));
  or or_1 (or_1_out[0], Q0W, Q0R);
  xor xor_1 (xor_1_out, READ_out, Write_out);
  xor xor_2 (xor_2_out, xor_1_out, Q1);
  D_Flip_Flop d_ff_1 (.D(xor_3_out), .clk(clock_1_out), .Q(Q1));  // open: Qn, preset, reset
  xor xor_3 (xor_3_out, Q1, Q0);
  D_Flip_Flop d_ff_2 (.D(and_1_out), .clk(clock_1_out), .Q(Q0), .Qn(d_ff_2_qn));  // open: preset, reset
  and and_1 (and_1_out, d_ff_2_qn, xor_2_out);
  RAM #(.addrWidth(10), .dataWidth(4), .databus("bidir"), .trigger("high")) ram_1 (
    .addr({{9{1'b0}}, or_1_out[0]}), .we(Q1W), .oe(not_1_out), .data(ram_1_data));
  not not_1 (not_1_out, Q1W);
  assign ram_1_data[3] = Q1W ? multiplexer_1_out : 1'bz;  // Controlled_Buffer controlled_buffer_1
  assign ram_1_data[2] = Q1W ? multiplexer_2_out : 1'bz;  // Controlled_Buffer controlled_buffer_2
  assign ram_1_data[1] = Q1W ? multiplexer_3_out : 1'bz;  // Controlled_Buffer controlled_buffer_3
  assign ram_1_data[0] = Q1W ? multiplexer_4_out : 1'bz;  // Controlled_Buffer controlled_buffer_4
  Register #(.width(4)) RegisterA (.D(ram_1_data), .clk(undriven), .Q(RegisterA_q));  // open: en, clr
  Register #(.width(4)) RegisterB (.D(ram_1_data), .clk(not_2_out), .Q(RegisterB_q));  // open: en, clr
  not not_2 (not_2_out, undriven);
  LED led_1 (.in(RegisterA_q[0]));
  LED led_2 (.in(RegisterA_q[1]));
  LED led_3 (.in(RegisterA_q[2]));
  LED led_4 (.in(RegisterA_q[3]));
  LED led_5 (.in(RegisterB_q[0]));
  LED led_6 (.in(RegisterB_q[1]));
  LED led_7 (.in(RegisterB_q[2]));
  LED led_8 (.in(RegisterB_q[3]));
endmodule
